// Logisim project 1.circ as structural Verilog: 1 circuit, main circuit main
module main (
  input  A,
  input  B,
  input  A_2,
  input  B_2,
  input  A_3,
  input  A_4,
  input  B_3,
  input  A_5,
  input  B_4,
  output Y_AB,
  output Y_A_B,
  output Y_A_prime,
  output Y_A_prime_B_AB_prime,
  output Y_AB_A_prime_B_prime
);

  not not_1 (Y_A_prime, A_3);
  and and_1 (Y_AB, A, B);
  or or_1 (Y_A_B, A_2, B_2);
  xor xor_1 (Y_A_prime_B_AB_prime, A_4, B_3);
  xnor xnor_1 (Y_AB_A_prime_B_prime, A_5, B_4);
endmodule
